# Fritzing sketch SmartPillBoxDiagram1 (saved by Fritzing 1.0.6)

parts:
  J1 = Basic Servo
  M1 = DOIT Esp32 DevKit v1 (30 pins long, 11 pins width) [part_number=ESP32S-PIN30]
  Driver2 = 28BYJ-48 Driver Module [part_number=ULN2003 package=THT]
  SM2 = 28BYJ-48 Stepper Motor [part_number=28BYJ-48]
  Skip_Button = Momentary Switch [package=ksa_sealed_tac_switch]
  Take_Button = Momentary Switch [package=ksa_sealed_tac_switch]
  S3 = Toggle Switch [package=THT]
  M2 = RioRand LM2596
  BAT1 = 18650 battery holder [package=battery-18650-kit]
  BAT2 = 18650 battery holder [package=battery-18650-kit]
  Mod1 = KY-015 Temperature & Humidity Sensor Module [package="Breakout board"]
  J2 = Piezo Speaker

nets (from the schematic view):
  GND: J1.gnd, M1.GND, Driver2.GND, Skip_Button.4, Take_Button.4, M2.Pin_4, Mod1.-, J2.pin1
  VIN: J1.vcc, M1.VIN, Driver2.Vmotor, M2.Pin_3, Mod1.Vin
  N1: J1.pulse, M1.D13
  N2: M1.D2, Mod1.S
  N3: M1.D5, Driver2.IN2
  N4: M1.D18, Driver2.IN3
  N5: M1.D19, Driver2.IN1
  N6: M1.D26, Take_Button.2
  N7: M1.D27, Driver2.IN4
  N8: M1.D14, Skip_Button.2
  N9: M1.D12, J2.pin2
  N10: Driver2.blue-pin, SM2.blue-pin
  N11: Driver2.pink-pin, SM2.pink-pin
  N12: Driver2.yellow-pin, SM2.yellow-pin
  N13: Driver2.orange-pin, SM2.orange-pin
  N14: Driver2.red-pin, SM2.red-pin
  N15: S3.COM, BAT2.+
  N16: S3.L2, M2.Pin_1
  N17: M2.Pin_2, BAT1.-
  N18: BAT1.+, BAT2.-

notes:
  rid Servo
  Pills Slot Rotator
  Take / Skip Button
  Temperature and Humidity Sensor
  Power Unit
  The Brian (ESP-32)

custom parts:
  DOIT Esp32 DevKit v1 (30 pins long, 11 pins width): The DOIT Esp32 DevKit v1 is one of the development board created by DOIT to evaluate the ESP-WROOM-32 module. It is based on the ESP32 microcontroller that boasts Wifi, Bluetooth, Ethernet and Low Power support all in a single chip. (vanepp) made breadboard work, adjusted pin numbering and labels and reduced size of schematic and cleaned up pcb. This chip is 30pins long (2 x15) and 11 pins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
  28BYJ-48 Driver Module: Generic male header
  28BYJ-48 Stepper Motor: Unipolar Stepper Motor 28BYJ-48 Top coil - pink & orange Bottom coil - blue & yellow Common rail - red Connector pins: blue - pink - yellow - orange - red
  18650 battery holder: 18650 Battery Holder identical to the dual battery version.
  KY-015 Temperature & Humidity Sensor Module: KY-015 temperature and humidity sensor module, provides a low-latency serial interface to measure humidity and temperature.
